# Fritzing sketch growbox_shema (saved by Fritzing 0.9.3b)
circuit board: 7.37852cm x 5.22369cm

parts:
  Grove1 = Grove OLED 128x96
  Gnd_Temp_1 = DS18B20 1-Wire Temperature Sensor [part_number=DS18B20]
  Arduino_Nano = Arduino Nano (Rev3.0)
  Air_Temp_Humidity = BME280 Breakout
  Gnd_Temp_1_2 = DS18B20 1-Wire Temperature Sensor [part_number=DS18B20]
  R1 = Resistor [tolerance=±5% resistance=4.7k package=THT]

nets:
  GND: Grove1.GND, Gnd_Temp_1.GND, Arduino_Nano.GND, Air_Temp_Humidity.GND, Gnd_Temp_1_2.GND
  VDD: Grove1.VCC, Gnd_Temp_1.VDD, Arduino_Nano.5V, Air_Temp_Humidity.3.3V, Gnd_Temp_1_2.VDD, R1.Pin_1
  N1: Grove1.SDA, Arduino_Nano.A4, Air_Temp_Humidity.SDI/SDA
  N2: Grove1.SCL, Arduino_Nano.A5, Air_Temp_Humidity.SCK/SCL
  N3: Gnd_Temp_1.DQ, Arduino_Nano.D2, Gnd_Temp_1_2.DQ, R1.Pin_0
